// Logisim project tp1.circ as structural Verilog
module exercice1 (
  input  a,
  input  b,
  output out_3
);

  wire and_1_out, and_2_out, not_1_out;

  not not_1 (not_1_out, a);
  and and_1 (and_1_out, a, b);
  and and_2 (and_2_out, not_1_out, b);
  or or_1 (out_3, and_1_out, and_2_out);
endmodule

module decodeur (
  input  in_1,
  input  in_2,
  input  in_3,
  output _0,
  output _1,
  output _2,
  output _3,
  output _4,
  output _5,
  output _6
);

  wire not_1_out, not_2_out, not_3_out, not_4_out, not_5_out, not_6_out, not_7_out, not_8_out, not_9_out,
       not_10_out, not_11_out;

  not not_1 (not_1_out, in_1);
  not not_2 (not_2_out, in_2);
  not not_3 (not_3_out, in_3);
  not not_4 (not_4_out, in_1);
  not not_5 (not_5_out, in_2);
  not not_6 (not_6_out, in_1);
  not not_7 (not_7_out, in_3);
  not not_8 (not_8_out, in_2);
  not not_9 (not_9_out, in_3);
  not not_10 (not_10_out, in_2);
  not not_11 (not_11_out, in_3);
  and and_1 (_0, not_1_out, not_2_out, not_3_out);
  and and_2 (_1, not_4_out, not_5_out, in_3);
  and and_3 (_2, not_6_out, in_2, not_7_out);
  and and_4 (_3, in_1, not_8_out, not_9_out);
  and and_5 (_4, in_1, not_10_out, in_3);
  and and_6 (_5, in_1, in_2, not_11_out);
  and and_7 (_6, in_1, in_2, in_3);
endmodule

module afficheur (
  input  in_1,
  input  in_2,
  input  in_3
);

  wire decodeur_1__0, decodeur_1__1, decodeur_1__2, decodeur_1__3, decodeur_1__4, decodeur_1__5,
       decodeur_1__6, or_1_out, or_2_out, or_3_out, or_4_out, or_5_out, or_6_out, or_7_out;

  decodeur decodeur_1 (
    .in_1(in_1), .in_2(in_2), .in_3(in_3), ._0(decodeur_1__0), ._1(decodeur_1__1), ._2(decodeur_1__2),
    ._3(decodeur_1__3), ._4(decodeur_1__4), ._5(decodeur_1__5), ._6(decodeur_1__6));
  or or_1 (or_1_out, decodeur_1__0, decodeur_1__1, decodeur_1__2, decodeur_1__3, decodeur_1__4);
  or or_2 (or_2_out, decodeur_1__0, decodeur_1__2, decodeur_1__3, decodeur_1__5, decodeur_1__6);
  or or_3 (or_3_out, decodeur_1__0, decodeur_1__4, decodeur_1__5, decodeur_1__6);
  or or_4 (or_4_out, decodeur_1__2, decodeur_1__3, decodeur_1__4, decodeur_1__5, decodeur_1__6);
  or or_5 (or_5_out, decodeur_1__0, decodeur_1__2, decodeur_1__6);
  or or_6 (or_6_out, decodeur_1__0, decodeur_1__2, decodeur_1__3, decodeur_1__5, decodeur_1__6);
  or or_7 (or_7_out, decodeur_1__0, decodeur_1__1, decodeur_1__3, decodeur_1__4, decodeur_1__5, decodeur_1__6);
  _7_Segment_Display u_7_segment_display_1 (
    .g(or_4_out), .f(or_3_out), .a(or_2_out), .b(or_1_out), .e(or_5_out), .d(or_6_out), .c(or_7_out));  // open: dp

  // Notes on the sheet:
  //   4
  //   3
  //   2
  //   1
  //   5
  //   6
  //   7
endmodule
